// Logisim project cse332_project.circ as structural Verilog
module main (
  input  Write_Enable,
  input  Cin,
  input  B_invert,
  input  [2:0] operation,
  input  Reg_Dst,
  input  MemToReg,
  input  ALUSrc,
  input  sw,
  input  lw,
  input  SLL_SRL,
  input  Shift,
  output [15:0] read_data_1,
  output [15:0] \output ,
  output [15:0] read_data_2,
  output [3:0] opcode,
  output [3:0] RS,
  output [3:0] RT,
  output [3:0] RD,
  output zero,
  output overflow,
  output Cout
);

  wire clock, reset;
  wire [3:0] RD_RT;
  wire [15:0] adder_1_out, Data, imm, RAM_data, Reg_Imm, register_1_q, shifted_value, Write_Data;

  Clock u_clock (.out(clock));
  Button u_reset (.out(reset));
  Adder #(.width(16)) adder_1 (.a(register_1_q), .b(16'h1), .out(adder_1_out));  // open: cin, cout
  Multiplexer #(.width(4)) multiplexer_1 (.in0(RD), .in1(RT), .out(RD_RT), .sel(Reg_Dst));  // open: en
  Multiplexer #(.width(16)) multiplexer_2 (.in0(\output ), .in1(RAM_data), .out(Data), .sel(MemToReg));  // open: en
  Register #(.width(16)) register_1 (.D(adder_1_out), .Q(register_1_q), .clk(clock), .clr(reset));  // open: en
  Multiplexer #(.width(16)) multiplexer_3 (.in0(read_data_2), .in1(imm), .out(Reg_Imm), .sel(ALUSrc));  // open: en
  Multiplexer #(.width(16)) multiplexer_4 (.in0(Data), .in1(shifted_value), .out(Write_Data), .sel(Shift));  // open: en
  ROM #(.addrWidth(16), .dataWidth(16)) rom_1 (.addr(register_1_q), .data({opcode, RS, RT, RD}));  // open: sel
  assign imm = {{12{1'b0}}, RD};  // Bit_Extender bit_extender_1
  RAM #(.addrWidth(16), .dataWidth(16), .bus("separate")) ram_1 (
    .addr(\output ), .din(read_data_2), .data(RAM_data), .str(sw), .clk(clock), .ld(lw), .clr(reset));  // open: sel
  _16_bit_register_file_ic_with_zero u_16_bit_register_file_ic_with_zero_1 (
    .Write_Data(Write_Data), .Write_Enable(Write_Enable), .RS(RS), .RT(RT), .Read_Data_1(read_data_1),
    .Read_Data_2(read_data_2), .Clock(clock), .Reset(reset), .Destination__RD(RD_RT));
  Shift shift_1 (.Data(read_data_1), .Shift_ammount(RD), .SLL_SRL(SLL_SRL), .Output(shifted_value));
  _16_bit_alu u_16_bit_alu_1 (
    .B_invert(B_invert), .Cin(Cin), .Output(operation), .A(read_data_1), .B(Reg_Imm), .output_2(\output ),
    .zero(zero), .Cout(Cout), .overflow(overflow));

  // Other names for the same wires on the sheet: Write_En = Write_Enable

  // Notes on the sheet:
  //   contents of rom_1 (hex, n*v repeats v):
  //   1234
endmodule

module _16bit_register_file_ic (
  input  Clock,
  input  Reset,
  input  [15:0] Write_Data,
  input  Write_Enable,
  input  [3:0] Destination__RD,
  input  [3:0] RS,
  input  [3:0] RT,
  output [15:0] Read_Data_1,
  output [15:0] Read_Data_2
);

  wire demultiplexer_1_out0, demultiplexer_1_out1, demultiplexer_1_out2, demultiplexer_1_out3,
       demultiplexer_1_out4, demultiplexer_1_out5, demultiplexer_1_out6, demultiplexer_1_out7,
       demultiplexer_1_out8, demultiplexer_1_out9, demultiplexer_1_out10, demultiplexer_1_out11,
       demultiplexer_1_out12, demultiplexer_1_out13, demultiplexer_1_out14, demultiplexer_1_out15;
  wire [15:0] r0_q, r1_q, r2_q, r3_q, r4_q, r5_q, r6_q, r7_q, r8_q, r9_q, r10_q, r11_q, r12_q, r13_q, r14_q,
       r15_q;

  Demultiplexer #(.select(4)) demultiplexer_1 (
    .out0(demultiplexer_1_out0), .out1(demultiplexer_1_out1), .out2(demultiplexer_1_out2),
    .out3(demultiplexer_1_out3), .out4(demultiplexer_1_out4), .out5(demultiplexer_1_out5),
    .out6(demultiplexer_1_out6), .out7(demultiplexer_1_out7), .out8(demultiplexer_1_out8),
    .out9(demultiplexer_1_out9), .out10(demultiplexer_1_out10), .out11(demultiplexer_1_out11),
    .out12(demultiplexer_1_out12), .out13(demultiplexer_1_out13), .out14(demultiplexer_1_out14),
    .out15(demultiplexer_1_out15), .in(Write_Enable), .sel(Destination__RD));  // open: en
  Register #(.width(16)) r0 (.D(Write_Data), .en(demultiplexer_1_out0), .Q(r0_q), .clk(Clock), .clr(Reset));
  Register #(.width(16)) r1 (.D(Write_Data), .en(demultiplexer_1_out1), .Q(r1_q), .clk(Clock), .clr(Reset));
  Register #(.width(16)) r2 (.D(Write_Data), .en(demultiplexer_1_out2), .Q(r2_q), .clk(Clock), .clr(Reset));
  Register #(.width(16)) r3 (.D(Write_Data), .en(demultiplexer_1_out3), .Q(r3_q), .clk(Clock), .clr(Reset));
  Register #(.width(16)) r4 (.D(Write_Data), .en(demultiplexer_1_out4), .Q(r4_q), .clk(Clock), .clr(Reset));
  Register #(.width(16)) r5 (.D(Write_Data), .en(demultiplexer_1_out5), .Q(r5_q), .clk(Clock), .clr(Reset));
  Register #(.width(16)) r6 (.D(Write_Data), .en(demultiplexer_1_out6), .Q(r6_q), .clk(Clock), .clr(Reset));
  Register #(.width(16)) r7 (.D(Write_Data), .en(demultiplexer_1_out7), .Q(r7_q), .clk(Clock), .clr(Reset));
  Register #(.width(16)) r8 (.D(Write_Data), .en(demultiplexer_1_out8), .Q(r8_q), .clk(Clock), .clr(Reset));
  Register #(.width(16)) r9 (.D(Write_Data), .en(demultiplexer_1_out9), .Q(r9_q), .clk(Clock), .clr(Reset));
  Register #(.width(16)) r10 (.D(Write_Data), .en(demultiplexer_1_out10), .Q(r10_q), .clk(Clock), .clr(Reset));
  Register #(.width(16)) r11 (.D(Write_Data), .en(demultiplexer_1_out11), .Q(r11_q), .clk(Clock), .clr(Reset));
  Register #(.width(16)) r12 (.D(Write_Data), .en(demultiplexer_1_out12), .Q(r12_q), .clk(Clock), .clr(Reset));
  Register #(.width(16)) r13 (.D(Write_Data), .en(demultiplexer_1_out13), .Q(r13_q), .clk(Clock), .clr(Reset));
  Register #(.width(16)) r14 (.D(Write_Data), .en(demultiplexer_1_out14), .Q(r14_q), .clk(Clock), .clr(Reset));
  Register #(.width(16)) r15 (.D(Write_Data), .en(demultiplexer_1_out15), .Q(r15_q), .clk(Clock), .clr(Reset));
  Multiplexer #(.select(4), .width(16)) multiplexer_1 (
    .in0(r0_q), .in1(r1_q), .in2(r2_q), .in3(r3_q), .in4(r4_q), .in5(r5_q), .in6(r6_q), .in7(r7_q),
    .in8(r8_q), .in9(r9_q), .in10(r10_q), .in11(r11_q), .in12(r12_q), .in13(r13_q), .in14(r14_q),
    .in15(r15_q), .out(Read_Data_1), .sel(RS));  // open: en
  Multiplexer #(.select(4), .width(16)) multiplexer_2 (
    .in0(r0_q), .in1(r1_q), .in2(r2_q), .in3(r3_q), .in4(r4_q), .in5(r5_q), .in6(r6_q), .in7(r7_q),
    .in8(r8_q), .in9(r9_q), .in10(r10_q), .in11(r11_q), .in12(r12_q), .in13(r13_q), .in14(r14_q),
    .in15(r15_q), .out(Read_Data_2), .sel(RT));  // open: en
endmodule

module _16_bit_register_file_ic_with_zero (
  input  Clock,
  input  Reset,
  input  [15:0] Write_Data,
  input  Write_Enable,
  input  [3:0] Destination__RD,
  input  [3:0] RS,
  input  [3:0] RT,
  output [15:0] Read_Data_1,
  output [15:0] Read_Data_2
);

  wire demultiplexer_1_out0, demultiplexer_1_out1, demultiplexer_1_out2, demultiplexer_1_out3,
       demultiplexer_1_out4, demultiplexer_1_out5, demultiplexer_1_out6, demultiplexer_1_out7,
       demultiplexer_1_out8, demultiplexer_1_out9, demultiplexer_1_out10, demultiplexer_1_out11,
       demultiplexer_1_out12, demultiplexer_1_out13, demultiplexer_1_out14, demultiplexer_1_out15;
  wire [15:0] s0_q, s1_q, s2_q, s3_q, s4_q, s5_q, t0_q, t1_q, t2_q, t3_q, t4_q, t5_q, t6_q, t7_q, t8_q,
       zero_q;

  Demultiplexer #(.select(4)) demultiplexer_1 (
    .out0(demultiplexer_1_out0), .out1(demultiplexer_1_out1), .out2(demultiplexer_1_out2),
    .out3(demultiplexer_1_out3), .out4(demultiplexer_1_out4), .out5(demultiplexer_1_out5),
    .out6(demultiplexer_1_out6), .out7(demultiplexer_1_out7), .out8(demultiplexer_1_out8),
    .out9(demultiplexer_1_out9), .out10(demultiplexer_1_out10), .out11(demultiplexer_1_out11),
    .out12(demultiplexer_1_out12), .out13(demultiplexer_1_out13), .out14(demultiplexer_1_out14),
    .out15(demultiplexer_1_out15), .in(Write_Enable), .sel(Destination__RD));  // open: en
  Register #(.width(16)) zero (.D({16{1'b0}}), .en(demultiplexer_1_out0), .Q(zero_q), .clk(Clock), .clr(Reset));
  Register #(.width(16)) t0 (.D(Write_Data), .en(demultiplexer_1_out1), .Q(t0_q), .clk(Clock), .clr(Reset));
  Register #(.width(16)) t1 (.D(Write_Data), .en(demultiplexer_1_out2), .Q(t1_q), .clk(Clock), .clr(Reset));
  Register #(.width(16)) t2 (.D(Write_Data), .en(demultiplexer_1_out3), .Q(t2_q), .clk(Clock), .clr(Reset));
  Register #(.width(16)) t3 (.D(Write_Data), .en(demultiplexer_1_out4), .Q(t3_q), .clk(Clock), .clr(Reset));
  Register #(.width(16)) s0 (.D(Write_Data), .en(demultiplexer_1_out5), .Q(s0_q), .clk(Clock), .clr(Reset));
  Register #(.width(16)) s1 (.D(Write_Data), .en(demultiplexer_1_out6), .Q(s1_q), .clk(Clock), .clr(Reset));
  Register #(.width(16)) s2 (.D(Write_Data), .en(demultiplexer_1_out7), .Q(s2_q), .clk(Clock), .clr(Reset));
  Register #(.width(16)) s3 (.D(Write_Data), .en(demultiplexer_1_out8), .Q(s3_q), .clk(Clock), .clr(Reset));
  Register #(.width(16)) s4 (.D(Write_Data), .en(demultiplexer_1_out9), .Q(s4_q), .clk(Clock), .clr(Reset));
  Register #(.width(16)) s5 (.D(Write_Data), .en(demultiplexer_1_out10), .Q(s5_q), .clk(Clock), .clr(Reset));
  Register #(.width(16)) t4 (.D(Write_Data), .en(demultiplexer_1_out11), .Q(t4_q), .clk(Clock), .clr(Reset));
  Register #(.width(16)) t5 (.D(Write_Data), .en(demultiplexer_1_out12), .Q(t5_q), .clk(Clock), .clr(Reset));
  Register #(.width(16)) t6 (.D(Write_Data), .en(demultiplexer_1_out13), .Q(t6_q), .clk(Clock), .clr(Reset));
  Register #(.width(16)) t7 (.D(Write_Data), .en(demultiplexer_1_out14), .Q(t7_q), .clk(Clock), .clr(Reset));
  Register #(.width(16)) t8 (.D(Write_Data), .en(demultiplexer_1_out15), .Q(t8_q), .clk(Clock), .clr(Reset));
  Multiplexer #(.select(4), .width(16)) multiplexer_1 (
    .in0(zero_q), .in1(t0_q), .in2(t1_q), .in3(t2_q), .in4(t3_q), .in5(s0_q), .in6(s1_q), .in7(s2_q),
    .in8(s3_q), .in9(s4_q), .in10(s5_q), .in11(t4_q), .in12(t5_q), .in13(t6_q), .in14(t7_q), .in15(t8_q),
    .out(Read_Data_1), .sel(RS));  // open: en
  Multiplexer #(.select(4), .width(16)) multiplexer_2 (
    .in0(zero_q), .in1(t0_q), .in2(t1_q), .in3(t2_q), .in4(t3_q), .in5(s0_q), .in6(s1_q), .in7(s2_q),
    .in8(s3_q), .in9(s4_q), .in10(s5_q), .in11(t4_q), .in12(t5_q), .in13(t6_q), .in14(t7_q), .in15(t8_q),
    .out(Read_Data_2), .sel(RT));  // open: en
endmodule

module _1bit_alu (
  input  B_prime,
  input  A,
  input  B,
  input  Cin,
  input  [2:0] Operation,
  output out_6,
  output out_7
);

  wire adder_1_cout, adder_1_out, and_1_out, multiplier_1_cout, multiplier_1_out, or_1_out, xor_1_out,
       xor_2_out;

  and and_1 (and_1_out, A, B);
  or or_1 (or_1_out, A, B);
  xor xor_1 (xor_1_out, B, B_prime);
  xor xor_2 (xor_2_out, A, B);
  Multiplier #(.width(1)) multiplier_1 (.a(A), .b(B), .out(multiplier_1_out), .cin(Cin), .cout(multiplier_1_cout));
  Adder #(.width(1)) adder_1 (.a(A), .b(xor_1_out), .out(adder_1_out), .cin(Cin), .cout(adder_1_cout));
  Multiplexer #(.select(3)) multiplexer_1 (
    .in0(and_1_out), .in1(or_1_out), .in2(adder_1_out), .in3(xor_2_out), .in4(multiplier_1_out), .in5(1'b0),
    .in6(1'b0), .in7(1'b0), .out(out_6), .sel(Operation));  // open: en
  Multiplexer #(.select(3)) multiplexer_2 (
    .in0(1'b0), .in1(1'b0), .in2(adder_1_cout), .in3(1'b0), .in4(multiplier_1_cout), .in5(1'b0), .in6(1'b0),
    .in7(1'b0), .out(out_7), .sel(Operation));  // open: en
endmodule

module Shift (
  input  [15:0] Data,
  input  [3:0] Shift_ammount,
  input  SLL_SRL,
  output [15:0] Output
);

  wire [15:0] shifter_1_out, shifter_2_out;

  Shifter #(.width(16)) shifter_1 (.in(Data), .\dist (Shift_ammount), .out(shifter_1_out));
  Shifter #(.width(16), .shift("lr")) shifter_2 (.in(Data), .\dist (Shift_ammount), .out(shifter_2_out));
  Multiplexer #(.width(16)) multiplexer_1 (
    .in0(shifter_1_out), .in1(shifter_2_out), .out(Output), .sel(SLL_SRL));  // open: en

  // Notes on the sheet:
  //   Shift Left Logical
  //   Shift Right Logical
endmodule

module _16_bit_alu (
  input  B_invert,
  input  Cin,
  input  [2:0] Output,
  input  [15:0] A,
  input  [15:0] B,
  output [15:0] output_2,
  output zero,
  output overflow,
  output Cout
);

  wire n1bit_alu_1_out_7, n1bit_alu_2_out_7, n1bit_alu_3_out_7, n1bit_alu_4_out_7, n1bit_alu_5_out_7,
       n1bit_alu_6_out_7, n1bit_alu_7_out_7, n1bit_alu_8_out_7, n1bit_alu_9_out_7, n1bit_alu_10_out_7,
       n1bit_alu_11_out_7, n1bit_alu_12_out_7, n1bit_alu_13_out_7, n1bit_alu_14_out_7, n1bit_alu_15_out_7;

  _1bit_alu u_1bit_alu_1 (
    .Operation(Output), .out_6(output_2[0]), .out_7(n1bit_alu_1_out_7), .B_prime(B_invert), .A(A[0]),
    .B(B[0]), .Cin(Cin));
  _1bit_alu u_1bit_alu_2 (
    .Operation(Output), .out_6(output_2[1]), .out_7(n1bit_alu_2_out_7), .B_prime(B_invert), .A(A[1]),
    .B(B[1]), .Cin(n1bit_alu_1_out_7));
  _1bit_alu u_1bit_alu_3 (
    .Operation(Output), .out_6(output_2[2]), .out_7(n1bit_alu_3_out_7), .B_prime(B_invert), .A(A[2]),
    .B(B[2]), .Cin(n1bit_alu_2_out_7));
  _1bit_alu u_1bit_alu_4 (
    .Operation(Output), .out_6(output_2[3]), .out_7(n1bit_alu_4_out_7), .B_prime(B_invert), .A(A[3]),
    .B(B[3]), .Cin(n1bit_alu_3_out_7));
  _1bit_alu u_1bit_alu_5 (
    .Operation(Output), .out_6(output_2[4]), .out_7(n1bit_alu_5_out_7), .B_prime(B_invert), .A(A[4]),
    .B(B[4]), .Cin(n1bit_alu_4_out_7));
  _1bit_alu u_1bit_alu_6 (
    .Operation(Output), .out_6(output_2[5]), .out_7(n1bit_alu_6_out_7), .B_prime(B_invert), .A(A[5]),
    .B(B[5]), .Cin(n1bit_alu_5_out_7));
  _1bit_alu u_1bit_alu_7 (
    .Operation(Output), .out_6(output_2[6]), .out_7(n1bit_alu_7_out_7), .B_prime(B_invert), .A(A[6]),
    .B(B[6]), .Cin(n1bit_alu_6_out_7));
  _1bit_alu u_1bit_alu_8 (
    .Operation(Output), .out_6(output_2[7]), .out_7(n1bit_alu_8_out_7), .B_prime(B_invert), .A(A[7]),
    .B(B[7]), .Cin(n1bit_alu_7_out_7));
  _1bit_alu u_1bit_alu_9 (
    .Operation(Output), .out_6(output_2[8]), .out_7(n1bit_alu_9_out_7), .B_prime(B_invert), .A(A[8]),
    .B(B[8]), .Cin(n1bit_alu_8_out_7));
  _1bit_alu u_1bit_alu_10 (
    .Operation(Output), .out_6(output_2[9]), .out_7(n1bit_alu_10_out_7), .B_prime(B_invert), .A(A[9]),
    .B(B[9]), .Cin(n1bit_alu_9_out_7));
  _1bit_alu u_1bit_alu_11 (
    .Operation(Output), .out_6(output_2[10]), .out_7(n1bit_alu_11_out_7), .B_prime(B_invert), .A(A[10]),
    .B(B[10]), .Cin(n1bit_alu_10_out_7));
  _1bit_alu u_1bit_alu_12 (
    .Operation(Output), .out_6(output_2[11]), .out_7(n1bit_alu_12_out_7), .B_prime(B_invert), .A(A[11]),
    .B(B[11]), .Cin(n1bit_alu_11_out_7));
  _1bit_alu u_1bit_alu_13 (
    .Operation(Output), .out_6(output_2[12]), .out_7(n1bit_alu_13_out_7), .B_prime(B_invert), .A(A[12]),
    .B(B[12]), .Cin(n1bit_alu_12_out_7));
  _1bit_alu u_1bit_alu_14 (
    .Operation(Output), .out_6(output_2[13]), .out_7(n1bit_alu_14_out_7), .B_prime(B_invert), .A(A[13]),
    .B(B[13]), .Cin(n1bit_alu_13_out_7));
  _1bit_alu u_1bit_alu_15 (
    .Operation(Output), .out_6(output_2[14]), .out_7(n1bit_alu_15_out_7), .B_prime(B_invert), .A(A[14]),
    .B(B[14]), .Cin(n1bit_alu_14_out_7));
  _1bit_alu u_1bit_alu_16 (
    .Operation(Output), .out_6(output_2[15]), .out_7(Cout), .B_prime(B_invert), .A(A[15]), .B(B[15]),
    .Cin(n1bit_alu_15_out_7));
  xor xor_1 (overflow, n1bit_alu_15_out_7, Cout);
  nor nor_1 (zero, output_2[0], output_2[1], output_2[2], output_2[3], output_2[4], output_2[5], output_2[6], output_2[7], output_2[8], output_2[9], output_2[10], output_2[11], output_2[12], output_2[13], output_2[14], output_2[15]);

  // Other names for the same wires on the sheet: _0 = output_2[0]; _1 = output_2[1]; _2 = output_2[2];
  //   _3 = output_2[3]; _4 = output_2[4]; _5 = output_2[5]; _6 = output_2[6]; _7 = output_2[7]; _8 = output_2[8];
  //   _9 = output_2[9]; _10 = output_2[10]; _11 = output_2[11]; _12 = output_2[12]; _13 = output_2[13];
  //   _14 = output_2[14]; _15 = output_2[15]
endmodule

module test_circuit (
  input  [3:0] in_1,
  input  [3:0] in_2,
  output [3:0] Cout,
  output [3:0] Cout_2
);

  Multiplier #(.width(4)) multiplier_1 (.a(in_1), .b(in_2), .out(Cout_2), .cout(Cout));  // open: cin

  // Notes on the sheet:
  //   110
endmodule
